# Fritzing sketch m4v06-2019 (saved by Fritzing 0.9.3b)
circuit board: 6.4cm x 7.9cm
breadboards: 1

parts:
  J1 = female pin header, 15 pins [form="♀ (female)"]
  Composant2 = Adafruit Feather M4 Express [part_number="Adafruit #3857"]
  J2 = female pin header, 15 pins [form="♀ (female)"]

nets:
  N1: J1.pin1, Composant2.D12, J2.pin1
  N2: J1.pin2, Composant2.D11, J2.pin2
  N3: J1.pin3, Composant2.D10, J2.pin3
  N4: J1.pin4, Composant2.D9, J2.pin4
  N5: J1.pin5, Composant2.D6, J2.pin5
  N6: J1.pin6, Composant2.D5, J2.pin6
  N7: J1.pin7, Composant2.D4, J2.pin7
  N8: J1.pin8, Composant2.A5, J2.pin8
  N9: J1.pin9, Composant2.A4, J2.pin9
  N10: J1.pin10, Composant2.A3, J2.pin10
  N11: J1.pin11, Composant2.A2, J2.pin11
  N12: J1.pin12, Composant2.A1, J2.pin12
  N13: J1.pin13, Composant2.A0, J2.pin13
  N14: J1.pin14, Composant2.GND, J2.pin14
  N15: J1.pin15, Composant2.+3V3, J2.pin15

notes:
  Lycée St Exupéry
  Olivier Boesch 2019
  M4 express PCB v1
  Marseille

custom parts:
  Adafruit Feather M4 Express: It's what you've been waiting for, the Feather M4 Express featuring ATSAMD51. This Feather is fast like a swift, smart like an owl, strong like a ox-bird (it's half ox, half bird, OK?) This feather is powered by our new favorite chip, the ATSAMD51J19 - with its 120MHz Cortex M4 with floating point support and 512KB Flash and 192KB RAM. Your code will zig and zag and zoom, and with a bunch of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
