# Fritzing sketch montage_angle (saved by Fritzing 0.9.3b)
breadboards: 1

parts:
  Composant1 = Adafruit Feather M4 Express [part_number="Adafruit #3857"]
  R1 = Resistor [tolerance=±5% resistance=10k package=THT]
  R2 = Rotary Potentiometer (Small) [maximum_resistance=100kΩ package=THT]

nets:
  N1: Composant1.A0, R1.Pin_0, R2.wiper
  N2: Composant1.GND, R1.Pin_1
  N3: Composant1.+3V3, R2.leg2

custom parts:
  Adafruit Feather M4 Express: It's what you've been waiting for, the Feather M4 Express featuring ATSAMD51. This Feather is fast like a swift, smart like an owl, strong like a ox-bird (it's half ox, half bird, OK?) This feather is powered by our new favorite chip, the ATSAMD51J19 - with its 120MHz Cortex M4 with floating point support and 512KB Flash and 192KB RAM. Your code will zig and zag and zoom, and with a bunch of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
